# Fritzing sketch WaterQuality (saved by Fritzing 0.9.5d)

parts:
  U1 = ESP32-38PinWide [part_number=ESP32-38PinWide]
  Componente1 = Adafruit SPI Flash SD Card [part_number="Adafruit #4899"]
  Componente2 = Adafruit 2.0 inch 240x320 IPS TFT [part_number="Adafruit #4311"]
  Componente4 = Adafruit ADS1115 16Bit I2C ADC [part_number="Adafruit #1085"]
  A1 = TS-300B interface
  A2 = TS 300B sensor
  DS1 = DS18B20 1-Wire Temperature Sensor Probe
  M1 = ph-4502c [package=THT]
  A3 = tds-sensor-meter-v1.0_1
  R1 = Resistor [tolerance=±5% resistance=4.7k package="1206 [SMD]"]
  TXS0108E_8-Bit_Bi-directional_Level-Shifting_Voltage_Translator1 = TXS0108 [part_number=TXS0108EPW package=TSSOP]
  S1 = Pushbutton [package="[THT]"]
  S2 = Pushbutton [package="[THT]"]
  S3 = Pushbutton [package="[THT]"]

nets:
  3.3V: U1.3.3, Componente1.3.3V, Componente2.BACKLIGHT, Componente2.3.3V, TXS0108E_8-Bit_Bi-directional_Level-Shifting_Voltage_Translator1.VccA, TXS0108E_8-Bit_Bi-directional_Level-Shifting_Voltage_Translator1.OE
  N1: U1.GPIO32, S1.Pin_1
  GND: U1.GPIO33, U1.GPIO25, U1.GND, Componente1.GND, Componente2.GND, Componente4.ADDR, Componente4.GND, A1.Pin_1, A1.Pin_8, A2.Pin_1, DS1.GND, M1.pin4, M1.pin5, A3.pin3, TXS0108E_8-Bit_Bi-directional_Level-Shifting_Voltage_Translator1.GND, S2.Pin_1, S2.Pin_2, S3.Pin_1, S3.Pin_2
  N2: U1.GPIO13, DS1.DQ, R1.Pin_0
  VDD: U1.VIN, Componente4.VDD, A1.Pin_4, DS1.VDD, M1.pin6, A3.pin2, TXS0108E_8-Bit_Bi-directional_Level-Shifting_Voltage_Translator1.VccB
  N3: U1.GPIO15, Componente1.SS
  N4: U1.GPIO4, Componente2.RESET_5V
  N5: U1.GPIO17, Componente2.DC_5V
  N6: U1.GPIO5, Componente2.LCDCS_5V
  N7: U1.GPIO18, Componente1.SCK, Componente2.MISO
  N8: U1.GPIO19, Componente1.MISO_3.3V
  N9: U1.GPIO21, TXS0108E_8-Bit_Bi-directional_Level-Shifting_Voltage_Translator1.A2
  N10: U1.GPIO22, TXS0108E_8-Bit_Bi-directional_Level-Shifting_Voltage_Translator1.A1
  N11: U1.GPIO23, Componente1.MOSI, Componente2.MOSI_5V
  N12: Componente4.AIN3, Componente4.AIN2, M1.pin3
  N13: Componente4.AIN1, A3.pin1
  N14: Componente4.AIN0, A1.Pin_2
  N15: Componente4.SDA, TXS0108E_8-Bit_Bi-directional_Level-Shifting_Voltage_Translator1.B2
  N16: Componente4.SCL, TXS0108E_8-Bit_Bi-directional_Level-Shifting_Voltage_Translator1.B1
  N17: A1.Pin_6, A2.Pin_3
  N18: A1.Pin_7, A2.Pin_2

custom parts:
  ESP32-38PinWide: Generic 38-Pin ESP32 with wide format (only access to one side of pins on a breadboard) based on Stephen Lilley's HiLetgo ESP-WROOM-32 ESP32 ESP-32S Development Board.
  Adafruit SPI Flash SD Card: This breakout is for a fascinating chip - it looks like an SPI Flash storage chip (like the GD25Q16) but its really an SD card, in an SMT chip format. What that means is that you wire up like an SD card breakout, and use the SD card libraries you already have for your microcontroller. For example, you can use the built in SD library in Arduino, or for CircuitPython we have an sdcard library.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
  Adafruit 2.0 inch 240x320 IPS TFT: This gorgeous IPS display breakout is the best way to add a small, colorful and bright display to any project, with excellent visibility from any angle. Since the display uses 4-wire SPI to communicate and has its own pixel-addressable frame buffer, it can be used with every kind of microcontroller. Even a very small one with low memory and few pins available! The 2.0" display has 320x240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
  Adafruit ADS1115 16Bit I2C ADC: For microcontrollers without an analog-to-digital converter or when you want a higher-precision ADC, the ADS1115 provides 16-bit precision at 860 samples/second over I2C. The chip can be configured as 4 single-ended input channels, or two differential channels. As a nice bonus, it even includes a programmable gain amplifier, up to x16, to help boost up smaller single/differential signals to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
  TS-300B interface: TS-300B interface.
  TS 300B sensor: TS 300B water turbidity sensor.
  ph-4502c: ph-4502c PH Meter.
  : TDS Meter V1.0 Development Board Water Meter Filter Measuring Water Sensor Module.
  TXS0108: This 8-bit non-inverting translator uses two separate configurable power-supply rails. The A port tracks the VCCA pin supply voltage. The VCCA pin accepts any supply voltage between 1.2 V and 3.6 V. The B port tracks the VCCB pin supply voltage. The VCCB pin accepts any supply voltage between 1.65 V and 5.5 V. Two input supply pins allows for low Voltage bidirectional translation between any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
